# Fritzing sketch sensor_luz_esquema (saved by Fritzing 0.9.2b)
breadboards: 1

parts:
  Componente1 = Arduino Uno (Rev3)
  R1 = Resistor [tolerance=±5% resistance=220 package=THT]
  R2 = Photocell (LDR) [package=THT]
  LED1 = LED - 5mm [color="Red (633nm)" package="5 mm [THT]"]
  R3 = Resistor [tolerance=±5% resistance=220 package=THT]
  R4 = Resistor [tolerance=±5% resistance=220 package=THT]
  D1 = LED_BARGRAPH_10 [package=led_bargaph_10]
  R5 = Resistor [tolerance=±5% resistance=220 package=THT]
  SG1 = Buzzer 12mm [package=buzzer-12mm-ns]
  R6 = Resistor [tolerance=±5% resistance=220 package=THT]

nets:
  N1: Componente1.A0, R1.Pin_1, R2.pin_0
  N2: Componente1.D8, D1.H_C
  N3: Componente1.D9_PWM, D1.I_C
  N4: Componente1.D10_PWM/SS, D1.J_C
  N5: Componente1.D11_PWM/MOSI, R6.Pin_0
  N6: Componente1.D13/SCK, R4.Pin_0
  N7: Componente1.D5_PWM, D1.E_C
  N8: Componente1.D6_PWM, D1.F_C
  N9: Componente1.D7, D1.G_C
  N10: Componente1.5V, R2.pin_1, LED1.anode, R5.Pin_1, SG1.2
  N11: Componente1.GND, R1.Pin_0
  N12: LED1.cathode, R3.Pin_1
  N13: R3.Pin_0, R4.Pin_1
  N14: D1.E_A, D1.F_A, D1.G_A, D1.H_A, D1.I_A, D1.J_A, R5.Pin_0
  N15: SG1.1, R6.Pin_1
